// Logisim project ex4.circ as structural Verilog: 1 circuit, main circuit Split
module Split (
  input  [7:0] In1,
  output Out1,
  output [7:0] Out2
);

  wire [7:0] not_1_out;

  assign not_1_out = ~In1;  // NOT_Gate not_1, 8 bits wide
  and and_1 (Out1, In1[0], In1[7]);
  Adder adder_1 (.a(not_1_out), .b(8'h1), .out(Out2));  // open: cin, cout

  // Notes on the sheet:
  //   PUT CIRCUITRY HERE
endmodule
